# Fritzing sketch open-race-scale-pi-hat-v1 (saved by Fritzing 0.9.3b)
circuit board: 8.53488cm x 5.63626cm

parts:
  LC1 = HX711 Weighing Sensor Module
  LC2 = HX711 Weighing Sensor Module
  LC3 = HX711 Weighing Sensor Module
  LC4 = HX711 Weighing Sensor Module
  FL = screw terminal, 4 pins
  FR = screw terminal, 4 pins
  RL = screw terminal, 4 pins
  RR = screw terminal, 4 pins
  3v = Pad [width=2 height=2 connect=center]
  P1 = Pad [width=2 height=2 connect=center]
  5v = Pad [width=2 height=2 connect=center]
  Ext = Pad [width=2 height=2 connect=center]
  P1_2 = Pad [width=2 height=2 connect=center]
  P0 = male pin header, 2 pins [form="♂ (male)"]
  J1 = male pin header, 3 pins [form="♂ (male)"]
  J2 = male pin header, 3 pins [form="♂ (male)"]
  Raspberry_Pi_1 = Raspberry Pi 3 [part_number=RPI-3-V1.2]
  J3 = male pin header, 3 pins [form="♂ (male)"]
  J4 = male pin header, 3 pins [form="♂ (male)"]
  J5 = male pin header, 3 pins [form="♂ (male)"]
  J6 = male pin header, 3 pins [form="♂ (male)"]
  J7 = male pin header, 3 pins [form="♂ (male)"]
  J8 = male pin header, 3 pins [form="♂ (male)"]

nets:
  VCC: LC1.VCC, LC2.VCC, LC3.VCC, LC4.VCC, P1.pad, 5v.pad, P1_2.pad, Raspberry_Pi_1.5V
  GND: LC1.GND, LC2.GND, LC3.GND, LC4.GND, P0.pin1, Raspberry_Pi_1.GND
  N1: LC1.DO/RX, Raspberry_Pi_1.GPIO17
  N2: LC1.CK/TX, Raspberry_Pi_1.GPIO27
  N3: LC1.E+, FL.pin4
  N4: LC1.E-, FL.pin3
  N5: LC1.A+, J1.pin1
  N6: LC1.A-, J2.pin1
  N7: LC1.B+, J1.pin3
  N8: LC1.B-, J2.pin3
  N9: LC2.DO/RX, Raspberry_Pi_1.GPIO22
  N10: LC2.CK/TX, Raspberry_Pi_1.GPIO23
  N11: LC2.E+, FR.pin4
  N12: LC2.E-, FR.pin3
  N13: LC2.A+, J3.pin1
  N14: LC2.A-, J4.pin1
  N15: LC2.B+, J3.pin3
  N16: LC2.B-, J4.pin3
  N17: LC3.DO/RX, Raspberry_Pi_1.GPIO5
  N18: LC3.CK/TX, Raspberry_Pi_1.GPIO6
  N19: LC3.E+, RL.pin4
  N20: LC3.E-, RL.pin3
  N21: LC3.A+, J5.pin1
  N22: LC3.A-, J6.pin1
  N23: LC3.B+, J5.pin3
  N24: LC3.B-, J6.pin3
  N25: LC4.DO/RX, Raspberry_Pi_1.GPIO16
  N26: LC4.CK/TX, Raspberry_Pi_1.GPIO26
  N27: LC4.E+, RR.pin4
  N28: LC4.E-, RR.pin3
  N29: LC4.A+, J7.pin1
  N30: LC4.A-, J8.pin1
  N31: LC4.B+, J7.pin3
  N32: LC4.B-, J8.pin3
  N33: FL.pin1, J2.pin2
  N34: FL.pin2, J1.pin2
  N35: FR.pin1, J4.pin2
  N36: FR.pin2, J3.pin2
  N37: RL.pin1, J6.pin2
  N38: RL.pin2, J5.pin2
  N39: RR.pin1, J8.pin2
  N40: RR.pin2, J7.pin2
  N41: 3v.pad, Raspberry_Pi_1.3v3
  5V: Ext.pad, P0.pin2

notes:
  Red -> E+
  Black -> E-
  Green -> A+
  White -> A-
  To FR Load Cell
  To RL Load Cell
  To RR Load Cell
  E+
  Ext Power
  (optional)
  Open Race Scale V1.0 Rev 02
  Gnd
  To FL Load Cell
  Jumper Pins to
  Select Channel
